# Fritzing sketch clock number 2 (saved by Fritzing 0.9.2b)
breadboards: 1

parts:
  Part1 = Arduino Uno (Rev3)
  LCD1 = LCD screen
  LED1 = LED - 5mm [color="Red (633nm)" package="5 mm [THT]"]
  LED2 = LED - 5mm [color="Red (633nm)" package="5 mm [THT]"]
  LED3 = LED - 5mm [color="Red (633nm)" package="5 mm [THT]"]
  LED4 = LED - 5mm [color="Red (633nm)" package="5 mm [THT]"]
  LED5 = LED - 5mm [color="Red (633nm)" package="5 mm [THT]"]
  LED6 = LED - 5mm [color="Blue (505nm)" package="5 mm [THT]"]
  LED7 = LED - 5mm [color="Blue (525nm)" package="5 mm [THT]"]
  LED8 = LED - 5mm [color="Blue (505nm)" package="5 mm [THT]"]
  LED9 = LED - 5mm [color="Blue (525nm)" package="5 mm [THT]"]
  LED10 = LED - 5mm [color="Blue (525nm)" package="5 mm [THT]"]
  R1 = Resistor [tolerance=±5% resistance=220 package=THT]
  R2 = Resistor [tolerance=±5% resistance=220 package=THT]
  R3 = Resistor [tolerance=±5% resistance=220 package=THT]
  R4 = Resistor [tolerance=±5% resistance=220 package=THT]
  R5 = Resistor [tolerance=±5% resistance=220 package=THT]
  R6 = Resistor [tolerance=±5% resistance=220 package=THT]
  R7 = Resistor [tolerance=±5% resistance=220 package=THT]
  R8 = Resistor [tolerance=±5% resistance=220 package=THT]
  R9 = Resistor [tolerance=±5% resistance=220 package=THT]
  R10 = Resistor [tolerance=±10% resistance=220 package=THT]
  T1 = LM35 Temperature Sensor [package="TO92 [THT]"]
  IC1 = DS1302 [package="SO8 [SMD]"]
  J1 = Piezo Speaker
  Part2 = Max Power IR LED Kit  # not connected

nets:
  N1: Part1.A0, T1.Vout
  N2: Part1.A1, LED3.anode
  N3: Part1.A2, LED4.anode
  N4: Part1.A3, LED5.anode
  N5: Part1.A4/SDA, LCD1.LED+
  N6: Part1.A5/SCL, LCD1.LED-
  N7: Part1.D9_PWM, LED1.anode
  N8: Part1.D10_PWM/SS, LED2.anode
  N9: Part1.D11_PWM/MOSI, LED7.anode
  N10: Part1.D12/MISO, J1.pin2
  N11: Part1.D13/SCK, LED6.anode
  N12: Part1.D2, LED10.anode
  N13: Part1.D3_PWM, LED9.anode
  N14: Part1.D4, LED8.anode
  5V: Part1.5V, LCD1.VSS, LCD1.VDD, T1.+Vs, IC1.+V, IC1.Vbat_-_Backup_Supply
  GND: Part1.GND, R1.Pin_1, R2.Pin_1, R3.Pin_1, R4.Pin_1, R5.Pin_1, R6.Pin_1, R7.Pin_1, R8.Pin_1, R9.Pin_1, R10.Pin_1, T1.GND, IC1.X1_-_Crystal, IC1.SCLK_-_SPI_Clock, J1.pin1
  N15: LED1.cathode, R5.Pin_0
  N16: LED2.cathode, R4.Pin_0
  N17: LED3.cathode, R3.Pin_0
  N18: LED4.cathode, R2.Pin_0
  N19: LED5.cathode, R1.Pin_0
  N20: LED6.cathode, R6.Pin_0
  N21: LED7.cathode, R7.Pin_0
  N22: LED8.cathode, R8.Pin_0
  N23: LED9.cathode, R9.Pin_0
  N24: LED10.cathode, R10.Pin_0
  N25: IC1.X2_-_Crystal, IC1.I/O_-_SPI_Data_In/Out
  N26: IC1.0V, IC1.CE_-_Chip_Enable
